# Fritzing sketch Esquema_Braco_Robotico (saved by Fritzing 0.9.10b)
breadboards: 1

parts:
  Componente1 = Arduino Uno (Rev3)
  J1 = Basic Servo
  Componente4 = Thumb Joystick
  Componente2 = Thumb Joystick
  J2 = Basic Servo
  J3 = Basic Servo
  J4 = Basic Servo

nets:
  N1: Componente1.A0, Componente4.VERT
  N2: Componente1.A1, Componente4.HORZ
  N3: Componente1.A2, Componente2.VERT
  N4: Componente1.A3, Componente2.HORZ
  N5: Componente1.D9_PWM, J3.pulse
  N6: Componente1.D10_PWM/SS, J4.pulse
  N7: Componente1.D5_PWM, J1.pulse
  N8: Componente1.D6_PWM, J2.pulse
  VCC: Componente1.5V, J1.vcc, Componente4.VCC, Componente2.VCC, J2.vcc, J3.vcc, J4.vcc
  GND: Componente1.GND, J1.gnd, Componente4.GND, Componente2.GND, J2.gnd, J3.gnd, J4.gnd
